# Fritzing sketch game_show_buzzer-teensy-protoboard-2 (saved by Fritzing 0.9.3b)
breadboards: 2
stripboards: 1

parts:
  R1 = Resistor [tolerance=±5% resistance=10k package=THT]
  R2 = Resistor [tolerance=±5% resistance=10k package=THT]
  R3 = Resistor [tolerance=±5% resistance=10k package=THT]
  R4 = Resistor [tolerance=±5% resistance=10k package=THT]
  R5 = Resistor [tolerance=±5% resistance=10k package=THT]
  R7 = Resistor [tolerance=±5% resistance=120 package=THT]
  R8 = Resistor [tolerance=±5% resistance=120 package=THT]
  R9 = Resistor [tolerance=±5% resistance=120 package=THT]
  J1 = Piezo Speaker
  R6 = Resistor [tolerance=±5% resistance=120 package=THT]
  Teensy_LC = Teensy-LC
  LED4 = LED - 5mm [color="Green (555nm)" package="5 mm [THT]"]
  LED3 = LED - 5mm [color="Yellow (595nm)" package="5 mm [THT]"]
  LED2 = LED - 5mm [color="Blue (470nm)" package="5 mm [THT]"]
  LED1 = LED - 5mm [color="Red (633nm)" package="5 mm [THT]"]
  J2 = RJ11 Jack [package=rj11-6]
  J3 = RJ11 Jack [package=rj11-6]
  J4 = RJ11 Jack [package=rj11-6]
  J5 = RJ11 Jack [package=rj11-6]
  J6 = RJ11 Jack [package=rj11-6]

nets:
  N1: R1.Pin_0, R2.Pin_0, R3.Pin_0, R4.Pin_0, R5.Pin_0, J1.pin1, Teensy_LC.GND, LED4.cathode, LED3.cathode, LED2.cathode, LED1.cathode, J2.2, J3.2, J4.2, J5.2, J6.2
  N2: R1.Pin_1, Teensy_LC.D2, J2.5
  N3: R2.Pin_1, Teensy_LC.D5, J3.5
  N4: R3.Pin_1, Teensy_LC.D7, J4.5
  N5: R4.Pin_1, Teensy_LC.D8, J5.5
  N6: R5.Pin_1, Teensy_LC.D10, J6.5
  N7: R7.Pin_0, Teensy_LC.D4
  N8: R7.Pin_1, LED2.anode
  N9: R8.Pin_0, Teensy_LC.D6
  N10: R8.Pin_1, LED3.anode
  N11: R9.Pin_0, Teensy_LC.D9
  N12: R9.Pin_1, LED4.anode
  N13: J1.pin2, Teensy_LC.A2/D16
  N14: R6.Pin_0, Teensy_LC.D3
  N15: R6.Pin_1, LED1.anode
  N16: Teensy_LC.5Vout, J2.3, J3.3, J4.3, J5.3, J6.3
  N17: Teensy_LC.3V3, J2.4, J3.4, J4.4, J5.4, J6.4

custom parts:
  Teensy-LC: Teensy-LC (Low Cost) is a powerful 32 bit microcontroller board, with a rich set of hardware peripherals, at a very affordable price! Teensy-LC delivers an impressive collection of capabilities to make modern electronic projects simpler. It features an ARM Cortex-M0+ processor at 48 MHz, 62K Flash, 8K RAM, 12 bit analog input & output, hardware Serial, SPI & I2C, USB, and a total of 27 I/O pins.
