# Fritzing sketch game_show_buzzer-teensy (saved by Fritzing 0.9.3b)
breadboards: 2

parts:
  S2 = Pushbutton [package="[THT]"]
  R1 = Resistor [tolerance=±5% resistance=10k package=THT]
  R2 = Resistor [tolerance=±5% resistance=10k package=THT]
  S1 = Pushbutton [package="[THT]"]
  S3 = Pushbutton [package="[THT]"]
  R3 = Resistor [tolerance=±5% resistance=10k package=THT]
  R4 = Resistor [tolerance=±5% resistance=10k package=THT]
  R5 = Resistor [tolerance=±5% resistance=10k package=THT]
  S4 = Pushbutton [package="[THT]"]
  S5 = Pushbutton [package="[THT]"]
  R7 = Resistor [tolerance=±5% resistance=120 package=THT]
  LED1 = LED - 5mm [color="Red (633nm)" package="5 mm [THT]"]
  LED2 = LED - 5mm [color="Red (633nm)" package="5 mm [THT]"]
  LED3 = LED - 5mm [color="Red (633nm)" package="5 mm [THT]"]
  LED4 = LED - 5mm [color="Red (633nm)" package="5 mm [THT]"]
  R8 = Resistor [tolerance=±5% resistance=120 package=THT]
  R9 = Resistor [tolerance=±5% resistance=120 package=THT]
  J1 = Piezo Speaker
  R6 = Resistor [tolerance=±5% resistance=120 package=THT]
  Teensy_LC = Teensy-LC

nets:
  N1: S2.Pin_1, S2.Pin_2, S1.Pin_1, S1.Pin_2, S3.Pin_1, S3.Pin_2, S4.Pin_1, S4.Pin_2, S5.Pin_1, S5.Pin_2, Teensy_LC.3V3
  N2: S2.Pin_3, S2.Pin_4, R2.Pin_1, Teensy_LC.D5
  N3: R1.Pin_0, R2.Pin_0, R3.Pin_0, R4.Pin_0, R5.Pin_0, LED1.cathode, LED2.cathode, LED3.cathode, LED4.cathode, J1.pin1, Teensy_LC.GND
  N4: R1.Pin_1, S1.Pin_3, S1.Pin_4, Teensy_LC.D2
  N5: S3.Pin_3, S3.Pin_4, R3.Pin_1, Teensy_LC.D7
  N6: R4.Pin_1, S4.Pin_3, S4.Pin_4, Teensy_LC.D8
  N7: R5.Pin_1, S5.Pin_3, S5.Pin_4, Teensy_LC.D10
  N8: R7.Pin_0, Teensy_LC.D4
  N9: R7.Pin_1, LED2.anode
  N10: LED1.anode, R6.Pin_1
  N11: LED3.anode, R8.Pin_1
  N12: LED4.anode, R9.Pin_1
  N13: R8.Pin_0, Teensy_LC.D6
  N14: R9.Pin_0, Teensy_LC.D9
  N15: J1.pin2, Teensy_LC.A2/D16
  N16: R6.Pin_0, Teensy_LC.D3

custom parts:
  Teensy-LC: Teensy-LC (Low Cost) is a powerful 32 bit microcontroller board, with a rich set of hardware peripherals, at a very affordable price! Teensy-LC delivers an impressive collection of capabilities to make modern electronic projects simpler. It features an ARM Cortex-M0+ processor at 48 MHz, 62K Flash, 8K RAM, 12 bit analog input & output, hardware Serial, SPI & I2C, USB, and a total of 27 I/O pins.
