# Fritzing sketch game_show_buzzer-uno (saved by Fritzing 0.9.3b)
breadboards: 1

parts:
  Arduino = Arduino Uno (Rev3)
  S3 = Pushbutton [package="[THT]"]
  R1 = Resistor [tolerance=±5% resistance=10k package=THT]
  R2 = Resistor [tolerance=±5% resistance=10k package=THT]
  S4 = Pushbutton [package="[THT]"]
  S2 = Pushbutton [package="[THT]"]
  R3 = Resistor [tolerance=±5% resistance=10k package=THT]
  R4 = Resistor [tolerance=±5% resistance=10k package=THT]
  R5 = Resistor [tolerance=±5% resistance=10k package=THT]
  S1 = Pushbutton [package="[THT]"]
  S5 = Pushbutton [package="[THT]"]
  R6 = Resistor [tolerance=±5% resistance=180 package=THT]
  R7 = Resistor [tolerance=±5% resistance=180 package=THT]
  LED1 = LED - 5mm [color="Red (633nm)" package="5 mm [THT]"]
  LED2 = LED - 5mm [color="Red (633nm)" package="5 mm [THT]"]
  LED3 = LED - 5mm [color="Red (633nm)" package="5 mm [THT]"]
  LED4 = LED - 5mm [color="Red (633nm)" package="5 mm [THT]"]
  R8 = Resistor [tolerance=±5% resistance=180 package=THT]
  R9 = Resistor [tolerance=±5% resistance=180 package=THT]
  J1 = Piezo Speaker

nets:
  N1: Arduino.D8, S3.Pin_3, S3.Pin_4, R2.Pin_1
  N2: Arduino.D9_PWM, R7.Pin_0
  N3: Arduino.D10_PWM/SS, R8.Pin_0
  N4: Arduino.D11_PWM/MOSI, R9.Pin_0
  N5: Arduino.D12/MISO, R1.Pin_1, S4.Pin_3, S4.Pin_4
  N6: Arduino.GND, R1.Pin_0, R2.Pin_0, R3.Pin_0, R4.Pin_0, R5.Pin_0, LED1.cathode, LED2.cathode, LED3.cathode, LED4.cathode, J1.pin1
  N7: Arduino.D2, R5.Pin_1, S5.Pin_3, S5.Pin_4
  N8: Arduino.D3_PWM, R6.Pin_0
  N9: Arduino.D4, R4.Pin_1, S1.Pin_3, S1.Pin_4
  N10: Arduino.D5_PWM, J1.pin2
  N11: Arduino.D7, S2.Pin_3, S2.Pin_4, R3.Pin_1
  N12: Arduino.5V, S3.Pin_1, S3.Pin_2, S4.Pin_1, S4.Pin_2, S2.Pin_1, S2.Pin_2, S1.Pin_1, S1.Pin_2, S5.Pin_1, S5.Pin_2
  N13: R6.Pin_1, LED1.anode
  N14: R7.Pin_1, LED2.anode
  N15: LED3.anode, R8.Pin_1
  N16: LED4.anode, R9.Pin_1
